# Fritzing sketch beed-room-clock-sketch (saved by Fritzing 0.9.4)
breadboards: 1

parts:
  M1 = DOIT Esp32 DevKit v1 (30 pins long, 11 pins width) [part_number=ESP32S-PIN30]
  hc-sr1 = hc-sr04
  DHT1 = DHT22 Humidity and Temperature Sensor
  R1 = Resistor [tolerance=±5% resistance=4.7k package="0402 [SMD]"]
  M2 = OLED Mono 2.42 inch green

nets:
  3V3: M1.3V3, DHT1.VDD, R1.Pin_1
  GND: M1.GND, hc-sr1.GND, DHT1.GND, M2.GND
  N1: M1.D15, M2.CS
  N2: M1.D4, DHT1.DATA, R1.Pin_0
  N3: M1.RX2, M2.DC
  N4: M1.TX2, M2.RES
  N5: M1.D5, hc-sr1.Trig
  N6: M1.D18, hc-sr1.Echo
  N7: M1.D14, M2.SCL
  N8: M1.D13, M2.SDA
  VCC: M1.VIN, hc-sr1.VCC, M2.VCC

custom parts:
  DOIT Esp32 DevKit v1 (30 pins long, 11 pins width): The DOIT Esp32 DevKit v1 is one of the development board created by DOIT to evaluate the ESP-WROOM-32 module. It is based on the ESP32 microcontroller that boasts Wifi, Bluetooth, Ethernet and Low Power support all in a single chip. (vanepp) made breadboard work, adjusted pin numbering and labels and reduced size of schematic and cleaned up pcb. This chip is 30pins long (2 x15) and 11 pins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
  OLED Mono 2.42 inch green: This is a 2.42 inch OLED display module of 128x64 resolution.
